# Fritzing sketch neildeighan-blog-pronguino-2-circuit-fritzing (saved by Fritzing 0.9.4)
circuit board: 7.1466cm x 7.01861cm
breadboards: 1

parts:
  Part1 = Arduino Uno (Rev3)
  R1 = Trimmer Potentiometer [maximum_resistance=10kΩ package=THT]
  R2 = Trimmer Potentiometer [maximum_resistance=10kΩ package=THT]

nets:
  N1: Part1.A1, R1.wiper
  N2: Part1.A2, R2.wiper
  N3: Part1.5V, R1.leg2, R2.leg2
  N4: Part1.GND, R1.leg1, R2.leg1
